// Logisim project Лабораторная_Работа_1_Кузнецов_БВТ2401.circ as structural Verilog: 1 circuit, main circuit main
module main (
  input  in_1,
  input  n,
  input  in_3,
  input  n_2,
  input  in_5,
  input  in_6,
  input  in_7,
  input  p,
  input  in_9,
  output \Вентиль_НЕ ,
  output out_11,
  output \Венитиль_И ,
  output \Вентиль_И_НЕ ,
  output \Вентиль_ИЛИ_НЕ 
);

  wire transistor_3_out, transistor_10_out, transistor_14_out, transistor_15_out;

  Transistor transistor_1 (.in(1'b1), .out(\Вентиль_НЕ ), .gate(in_5));
  Transistor #(.\type ("n")) transistor_2 (.in(1'b0), .out(\Вентиль_НЕ ), .gate(in_5));
  Transistor transistor_3 (.in(1'b1), .out(transistor_3_out), .gate(in_7));
  Transistor transistor_4 (.in(transistor_3_out), .out(\Вентиль_ИЛИ_НЕ ), .gate(in_9));
  Transistor #(.\type ("n")) transistor_5 (.in(1'b0), .out(\Вентиль_ИЛИ_НЕ ), .gate(in_9));
  Transistor #(.\type ("n")) transistor_6 (.in(1'b0), .out(\Вентиль_ИЛИ_НЕ ), .gate(in_7));
  Transistor #(.\type ("n")) transistor_7 (.in(1'b1), .out(out_11), .gate(n));
  Transistor #(.\type ("n")) transistor_8 (.in(1'b1), .out(out_11), .gate(in_3));
  Transistor transistor_9 (.in(transistor_10_out), .out(out_11), .gate(n));
  Transistor transistor_10 (.in(1'b0), .out(transistor_10_out), .gate(in_3));
  Transistor transistor_11 (.in(1'b1), .out(\Вентиль_И_НЕ ), .gate(in_6));
  Transistor transistor_12 (.in(1'b1), .out(\Вентиль_И_НЕ ), .gate(p));
  Transistor #(.\type ("n")) transistor_13 (.in(transistor_14_out), .out(\Вентиль_И_НЕ ), .gate(in_6));
  Transistor #(.\type ("n")) transistor_14 (.in(1'b0), .out(transistor_14_out), .gate(p));
  Transistor #(.\type ("n")) transistor_15 (.in(1'b1), .out(transistor_15_out), .gate(in_1));
  Transistor #(.\type ("n")) transistor_16 (.in(transistor_15_out), .out(\Венитиль_И ), .gate(n_2));
  Transistor transistor_17 (.in(1'b0), .out(\Венитиль_И ), .gate(in_1));
  Transistor transistor_18 (.in(1'b0), .out(\Венитиль_И ), .gate(n_2));

  // Notes on the sheet:
  //   p
  //   n
  //   p
  //   p
  //   n
  //   n
  //   n
  //   Вентиль ИЛИ
  //   р
  //   р
  //   p
  //   n
  //   n
  //   n
  //   p
  //   p
endmodule
