// Logisim project лаба2.circ as structural Verilog: 7 circuits, main circuit polusummator
module polusummator (
  input  A,
  input  B,
  output Sum,
  output CarryOut
);

  xor xor_1 (Sum, A, B);
  and and_1 (CarryOut, A, B);
endmodule

module summator (
  input  CI,
  input  a,
  input  b,
  output Sum,
  output CO
);

  wire polusummator_1_carryout, polusummator_1_sum, polusummator_2_carryout;

  polusummator polusummator_1 (.A(a), .B(b), .Sum(polusummator_1_sum), .CarryOut(polusummator_1_carryout));
  polusummator polusummator_2 (.A(CI), .B(polusummator_1_sum), .Sum(Sum), .CarryOut(polusummator_2_carryout));
  or or_1 (CO, polusummator_2_carryout, polusummator_1_carryout);

  // Notes on the sheet:
  //   полусумматор
  //   полусумматор
endmodule

module _8bitsumator (
  input  [7:0] in_1,
  input  [7:0] in_2,
  input  in_3,
  output [7:0] out_4,
  output out_5
);

  wire summator_1_co, summator_2_co, summator_3_co, summator_4_co, summator_5_co, summator_6_co,
       summator_7_co;

  // Probe on in_1
  // Probe on in_2
  summator summator_1 (.CI(in_3), .a(in_2[0]), .b(in_1[0]), .Sum(out_4[0]), .CO(summator_1_co));
  summator summator_2 (.CI(summator_1_co), .a(in_2[1]), .b(in_1[1]), .Sum(out_4[1]), .CO(summator_2_co));
  summator summator_3 (.CI(summator_2_co), .a(in_2[2]), .b(in_1[2]), .Sum(out_4[2]), .CO(summator_3_co));
  summator summator_4 (.CI(summator_3_co), .a(in_2[3]), .b(in_1[3]), .Sum(out_4[3]), .CO(summator_4_co));
  summator summator_5 (.CI(summator_4_co), .a(in_2[4]), .b(in_1[4]), .Sum(out_4[4]), .CO(summator_5_co));
  summator summator_6 (.CI(summator_5_co), .a(in_2[5]), .b(in_1[5]), .Sum(out_4[5]), .CO(summator_6_co));
  summator summator_7 (.CI(summator_6_co), .a(in_2[6]), .b(in_1[6]), .Sum(out_4[6]), .CO(summator_7_co));
  summator summator_8 (.CI(summator_7_co), .a(in_2[7]), .b(in_1[7]), .Sum(out_4[7]), .CO(out_5));
  // Probe on out_4

  // Notes on the sheet:
  //   сумматоры 
endmodule

module invertor (
  input  in_1,
  input  [7:0] in_2,
  output [7:0] out_3
);

  xor xor_1 (out_3[0], in_2[0], in_1);
  xor xor_2 (out_3[1], in_2[1], in_1);
  xor xor_3 (out_3[2], in_2[2], in_1);
  xor xor_4 (out_3[3], in_2[3], in_1);
  xor xor_5 (out_3[4], in_2[4], in_1);
  xor xor_6 (out_3[5], in_2[5], in_1);
  xor xor_7 (out_3[6], in_2[6], in_1);
  xor xor_8 (out_3[7], in_2[7], in_1);
endmodule

module vichitator (
  input  in_1,
  input  [7:0] in_2,
  input  [7:0] in_3,
  output [7:0] \сумматор ,
  output out_5
);

  wire [7:0] invertor_1_out_3;

  // Probe on in_2
  // Probe on in_3
  invertor invertor_1 (.in_2(in_3), .in_1(in_1), .out_3(invertor_1_out_3));
  _8bitsumator u_8bitsumator_1 (.in_1(in_2), .in_2(invertor_1_out_3), .in_3(in_1), .out_4(\сумматор ), .out_5(out_5));
  // Probe on \сумматор 

  // Notes on the sheet:
  //   инвертор
endmodule

module umnozhator (
  input  [3:0] in_1,
  input  [3:0] in_2,
  output [7:0] out_3
);

  wire and_1_out, and_2_out, and_3_out, and_4_out, and_5_out, and_6_out, and_7_out, and_8_out, and_9_out,
       and_10_out, and_11_out, and_12_out, and_13_out, and_14_out, and_16_out, summator_2_co, summator_2_sum,
       summator_3_co, summator_3_sum, summator_4_co, summator_4_sum, summator_5_co, summator_5_sum,
       summator_6_co, summator_7_co, summator_8_co, summator_8_sum, summator_9_co, summator_9_sum,
       summator_10_co, summator_11_co, summator_12_co;

  // Probe on in_1
  and and_1 (and_1_out, in_2[3], in_1[3]);
  summator summator_1 (.CI(summator_7_co), .a(and_1_out), .b(summator_4_co), .Sum(out_3[6]), .CO(out_3[7]));
  and and_2 (and_2_out, in_2[0], in_1[3]);
  and and_3 (and_3_out, in_2[1], in_1[2]);
  and and_4 (and_4_out, in_2[1], in_1[3]);
  summator summator_2 (.CI(summator_8_co), .a(and_3_out), .b(and_2_out), .Sum(summator_2_sum), .CO(summator_2_co));
  summator summator_3 (.CI(summator_2_co), .a(and_4_out), .b(1'b0), .Sum(summator_3_sum), .CO(summator_3_co));
  and and_5 (and_5_out, in_2[2], in_1[2]);
  and and_6 (and_6_out, in_2[2], in_1[3]);
  summator summator_4 (.CI(summator_5_co), .a(and_6_out), .b(summator_3_co), .Sum(summator_4_sum), .CO(summator_4_co));
  summator summator_5 (.CI(summator_9_co), .a(and_5_out), .b(summator_3_sum), .Sum(summator_5_sum), .CO(summator_5_co));
  and and_7 (and_7_out, in_2[3], in_1[1]);
  and and_8 (and_8_out, in_2[3], in_1[2]);
  summator summator_6 (.CI(summator_11_co), .a(and_7_out), .b(summator_5_sum), .Sum(out_3[4]), .CO(summator_6_co));
  summator summator_7 (.CI(summator_6_co), .a(and_8_out), .b(summator_4_sum), .Sum(out_3[5]), .CO(summator_7_co));
  and and_9 (and_9_out, in_2[0], in_1[1]);
  and and_10 (and_10_out, in_2[0], in_1[2]);
  and and_11 (and_11_out, in_2[1], in_1[1]);
  summator summator_8 (.CI(summator_12_co), .a(and_11_out), .b(and_10_out), .Sum(summator_8_sum), .CO(summator_8_co));
  and and_12 (and_12_out, in_2[2], in_1[0]);
  and and_13 (and_13_out, in_2[2], in_1[1]);
  summator summator_9 (
    .CI(summator_10_co), .a(and_13_out), .b(summator_2_sum), .Sum(summator_9_sum), .CO(summator_9_co));
  summator summator_10 (.CI(1'b0), .a(and_12_out), .b(summator_8_sum), .Sum(out_3[2]), .CO(summator_10_co));
  and and_14 (and_14_out, in_2[3], in_1[0]);
  summator summator_11 (.CI(1'b0), .a(and_14_out), .b(summator_9_sum), .Sum(out_3[3]), .CO(summator_11_co));
  and and_15 (out_3[0], in_2[0], in_1[0]);
  and and_16 (and_16_out, in_2[1], in_1[0]);
  summator summator_12 (.CI(1'b0), .a(and_16_out), .b(and_9_out), .Sum(out_3[1]), .CO(summator_12_co));
  // Probe on in_2
  // Probe on out_3
endmodule

module zadanie_1 (
  input  [1:0] in_1,
  input  [1:0] in_2,
  output [2:0] out_3
);

  wire summator_1_co;

  // Probe on in_1
  // Probe on in_2
  summator summator_1 (.CI(1'b0), .a(in_2[0]), .b(in_1[0]), .Sum(out_3[0]), .CO(summator_1_co));
  summator summator_2 (.CI(summator_1_co), .a(in_2[1]), .b(in_1[1]), .Sum(out_3[1]), .CO(out_3[2]));
  // Probe on out_3
endmodule
