// Logisim project Лаба3_Кузнецов_БВТ2401.circ as structural Verilog: 5 circuits, main circuit шифратор
module \шифратор  (
  input  _0,
  input  _1,
  input  _2,
  input  _3,
  input  _4,
  input  _5,
  input  _6,
  input  _7,
  input  _8,
  input  _9,
  input  _10,
  input  _11,
  input  _12,
  input  _13,
  input  _14,
  input  _15,
  output [3:0] out_17
);

  or or_1 (out_17[0], _1, _3, _5, _7, _9, _11, _13, _15);
  or or_2 (out_17[1], _2, _3, _6, _7, _10, _11, _14, _15);
  or or_3 (out_17[2], _4, _5, _6, _7, _12, _13, _14, _15);
  or or_4 (out_17[3], _8, _9, _10, _11, _12, _13, _14, _15);
  // Probe on out_17
endmodule

module \дешифратор  (
  input  [3:0] in_1,
  output _0,
  output _1,
  output _2,
  output _3,
  output _4,
  output _5,
  output _6,
  output _7,
  output _8,
  output _9,
  output _10,
  output _11,
  output _12,
  output _13,
  output _14,
  output _15
);

  wire not_1_out, not_2_out, not_3_out, not_4_out, not_5_out, not_6_out, not_7_out, not_8_out, not_9_out,
       not_10_out, not_11_out, not_12_out, not_13_out, not_14_out, not_15_out, not_16_out, not_17_out,
       not_18_out, not_19_out, not_20_out, not_21_out, not_22_out, not_23_out, not_24_out, not_25_out,
       not_26_out, not_27_out, not_28_out, not_29_out, not_30_out, not_31_out, not_32_out;

  // Probe on in_1
  not not_1 (not_1_out, in_1[0]);
  not not_2 (not_2_out, in_1[1]);
  and and_1 (_0, not_1_out, not_2_out, not_3_out, not_4_out);
  not not_3 (not_3_out, in_1[2]);
  not not_4 (not_4_out, in_1[3]);
  not not_5 (not_5_out, in_1[1]);
  and and_2 (_1, in_1[0], not_5_out, not_6_out, not_7_out);
  not not_6 (not_6_out, in_1[2]);
  not not_7 (not_7_out, in_1[3]);
  not not_8 (not_8_out, in_1[0]);
  and and_3 (_2, not_8_out, in_1[1], not_9_out, not_10_out);
  not not_9 (not_9_out, in_1[2]);
  not not_10 (not_10_out, in_1[3]);
  and and_4 (_3, in_1[0], in_1[1], not_11_out, not_12_out);
  not not_11 (not_11_out, in_1[2]);
  not not_12 (not_12_out, in_1[3]);
  not not_13 (not_13_out, in_1[0]);
  not not_14 (not_14_out, in_1[1]);
  and and_5 (_4, not_13_out, not_14_out, in_1[2], not_15_out);
  not not_15 (not_15_out, in_1[3]);
  not not_16 (not_16_out, in_1[1]);
  and and_6 (_5, in_1[0], not_16_out, in_1[2], not_17_out);
  not not_17 (not_17_out, in_1[3]);
  not not_18 (not_18_out, in_1[0]);
  and and_7 (_6, not_18_out, in_1[1], in_1[2], not_19_out);
  not not_19 (not_19_out, in_1[3]);
  and and_8 (_7, in_1[0], in_1[1], in_1[2], not_20_out);
  not not_20 (not_20_out, in_1[3]);
  not not_21 (not_21_out, in_1[0]);
  not not_22 (not_22_out, in_1[1]);
  and and_9 (_8, not_21_out, not_22_out, not_23_out, in_1[3]);
  not not_23 (not_23_out, in_1[2]);
  not not_24 (not_24_out, in_1[1]);
  and and_10 (_9, in_1[0], not_24_out, not_25_out, in_1[3]);
  not not_25 (not_25_out, in_1[2]);
  not not_26 (not_26_out, in_1[0]);
  and and_11 (_10, not_26_out, in_1[1], not_27_out, in_1[3]);
  not not_27 (not_27_out, in_1[2]);
  and and_12 (_11, in_1[0], in_1[1], not_28_out, in_1[3]);
  not not_28 (not_28_out, in_1[2]);
  not not_29 (not_29_out, in_1[0]);
  not not_30 (not_30_out, in_1[1]);
  and and_13 (_12, not_29_out, not_30_out, in_1[2], in_1[3]);
  not not_31 (not_31_out, in_1[1]);
  and and_14 (_13, in_1[0], not_31_out, in_1[2], in_1[3]);
  not not_32 (not_32_out, in_1[0]);
  and and_15 (_14, not_32_out, in_1[1], in_1[2], in_1[3]);
  and and_16 (_15, in_1[0], in_1[1], in_1[2], in_1[3]);
endmodule

module \мультиплексор  (
  input  in_1,
  input  in_2,
  input  in_3,
  input  in_4,
  input  in_5,
  input  in_6,
  output out_7
);

  wire and_1_out, and_2_out, and_3_out, and_4_out, not_1_out, not_2_out, not_3_out, not_4_out;

  not not_1 (not_1_out, in_5);
  not not_2 (not_2_out, in_6);
  not not_3 (not_3_out, in_5);
  not not_4 (not_4_out, in_6);
  and and_1 (and_1_out, not_1_out, not_2_out, in_1);
  and and_2 (and_2_out, not_3_out, in_6, in_2);
  and and_3 (and_3_out, in_5, not_4_out, in_3);
  and and_4 (and_4_out, in_5, in_6, in_4);
  or or_1 (out_7, and_1_out, and_2_out, and_3_out, and_4_out);
endmodule

module \демультиплексор  (
  input  in_1,
  input  in_2,
  input  in_3,
  output out_4,
  output out_5,
  output out_6,
  output out_7
);

  wire not_1_out, not_2_out, not_3_out, not_4_out;

  not not_1 (not_1_out, in_2);
  and and_1 (out_4, in_1, not_1_out, not_2_out);
  not not_2 (not_2_out, in_3);
  and and_2 (out_5, in_1, not_3_out, in_3);
  not not_3 (not_3_out, in_2);
  and and_3 (out_6, in_1, in_2, not_4_out);
  not not_4 (not_4_out, in_3);
  and and_4 (out_7, in_1, in_2, in_3);
endmodule

module \_7_сегментный  (
  input  _0,
  input  _1,
  input  _2,
  input  _3,
  input  _4,
  input  _5,
  input  _6,
  input  _7,
  input  _8,
  input  _9,
  input  A,
  input  B,
  input  C,
  input  D,
  input  E,
  input  F
);

  wire or_1_out, or_2_out, or_3_out, or_4_out, or_5_out, or_6_out, or_7_out, \дешифратор_1__0 ,
       \дешифратор_1__1 , \дешифратор_1__2 , \дешифратор_1__3 , \дешифратор_1__4 , \дешифратор_1__5 ,
       \дешифратор_1__6 , \дешифратор_1__7 , \дешифратор_1__8 , \дешифратор_1__9 , \дешифратор_1__10 ,
       \дешифратор_1__11 , \дешифратор_1__12 , \дешифратор_1__13 , \дешифратор_1__14 , \дешифратор_1__15 ;
  wire [3:0] \шифратор_1_out_17 ;

  \шифратор  \u_шифратор_1  (
    ._0(_0), ._1(_1), ._2(_2), ._3(_3), ._4(_4), ._5(_5), ._6(_6), ._7(_7), ._8(_8), ._9(_9), ._10(A),
    ._11(B), ._12(C), ._13(D), ._14(E), ._15(F), .out_17(\шифратор_1_out_17 ));
  \дешифратор  \u_дешифратор_1  (
    .in_1(\шифратор_1_out_17 ), ._0(\дешифратор_1__0 ), ._1(\дешифратор_1__1 ), ._2(\дешифратор_1__2 ),
    ._3(\дешифратор_1__3 ), ._4(\дешифратор_1__4 ), ._5(\дешифратор_1__5 ), ._6(\дешифратор_1__6 ),
    ._7(\дешифратор_1__7 ), ._8(\дешифратор_1__8 ), ._9(\дешифратор_1__9 ), ._10(\дешифратор_1__10 ),
    ._11(\дешифратор_1__11 ), ._12(\дешифратор_1__12 ), ._13(\дешифратор_1__13 ), ._14(\дешифратор_1__14 ),
    ._15(\дешифратор_1__15 ));
  or or_1 (or_1_out, \дешифратор_1__2 , \дешифратор_1__3 , \дешифратор_1__4 , \дешифратор_1__5 , \дешифратор_1__6 , \дешифратор_1__8 , \дешифратор_1__9 , \дешифратор_1__10 , \дешифратор_1__11 , \дешифратор_1__13 , \дешифратор_1__14 , \дешифратор_1__15 );
  or or_2 (or_2_out, \дешифратор_1__0 , \дешифратор_1__2 , \дешифратор_1__6 , \дешифратор_1__8 , \дешифратор_1__10 , \дешифратор_1__11 , \дешифратор_1__12 , \дешифратор_1__13 , \дешифратор_1__14 , \дешифратор_1__15 );
  or or_3 (or_3_out, \дешифратор_1__0 , \дешифратор_1__4 , \дешифратор_1__5 , \дешифратор_1__6 , \дешифратор_1__8 , \дешифратор_1__9 , \дешифратор_1__10 , \дешифратор_1__11 , \дешифратор_1__12 , \дешифратор_1__14 , \дешифратор_1__15 );
  _7_Segment_Display u_7_segment_display_1 (
    .g(or_1_out), .f(or_3_out), .a(or_5_out), .b(or_7_out), .e(or_2_out), .d(or_4_out), .c(or_6_out),
    .dp(1'b0));
  or or_4 (or_4_out, \дешифратор_1__0 , \дешифратор_1__2 , \дешифратор_1__3 , \дешифратор_1__5 , \дешифратор_1__6 , \дешифратор_1__8 , \дешифратор_1__9 , \дешифратор_1__11 , \дешифратор_1__12 , \дешифратор_1__13 , \дешифратор_1__14 );
  or or_5 (or_5_out, \дешифратор_1__0 , \дешифратор_1__2 , \дешифратор_1__3 , \дешифратор_1__5 , \дешифратор_1__6 , \дешифратор_1__7 , \дешифратор_1__8 , \дешифратор_1__9 , \дешифратор_1__10 , \дешифратор_1__12 , \дешифратор_1__14 , \дешифратор_1__15 );
  or or_6 (or_6_out, \дешифратор_1__0 , \дешифратор_1__1 , \дешифратор_1__3 , \дешифратор_1__4 , \дешифратор_1__5 , \дешифратор_1__6 , \дешифратор_1__7 , \дешифратор_1__8 , \дешифратор_1__9 , \дешифратор_1__10 , \дешифратор_1__11 , \дешифратор_1__13 );
  or or_7 (or_7_out, \дешифратор_1__0 , \дешифратор_1__1 , \дешифратор_1__2 , \дешифратор_1__3 , \дешифратор_1__4 , \дешифратор_1__7 , \дешифратор_1__8 , \дешифратор_1__9 , \дешифратор_1__10 , \дешифратор_1__13 );
endmodule
