// Logisim project Лабораторная 4.circ as structural Verilog: 10 circuits, main circuit Асинхронный RS триггер
module \Асинхронный_RS_триггер  (
  input  Reset,
  input  Set,
  output out_3,
  output out_4
);

  and and_1 (out_3, ~Reset, ~out_4);  // AND_Gate
  and and_2 (out_4, ~out_3, ~Set);  // AND_Gate
endmodule

module \Синхронный_RS_триггер  (
  input  Reset,
  input  Clock,
  input  Set,
  output out_4,
  output out_5
);

  wire and_1_out, and_2_out;

  and and_1 (and_1_out, Reset, Clock);
  and and_2 (and_2_out, Clock, Set);
  nor nor_1 (out_4, and_1_out, out_5);
  nor nor_2 (out_5, out_4, and_2_out);
endmodule

module \JK_триггер  (
  input  Jump,
  input  Clock,
  input  Kill,
  output out_4,
  output out_5
);

  wire nand_1_out, nand_2_out, nand_3_out, nand_4_out, nand_5_out, nand_6_out;

  nand nand_1 (nand_1_out, out_5, Jump, Clock);
  nand nand_2 (nand_2_out, Clock, Kill, out_4);
  nand nand_3 (nand_3_out, nand_1_out, nand_4_out);
  nand nand_4 (nand_4_out, nand_3_out, nand_2_out);
  nand nand_5 (nand_5_out, nand_1_out, nand_3_out);
  nand nand_6 (nand_6_out, nand_4_out, nand_2_out);
  nand nand_7 (out_4, nand_5_out, out_5);
  nand nand_8 (out_5, out_4, nand_6_out);
endmodule

module \D_триггер  (
  input  Clear,
  input  Clock,
  input  Data,
  output out_4,
  output out_5
);

  wire and_1_out, and_2_out, not_1_out, or_1_out;

  not not_1 (not_1_out, Data);
  and and_1 (and_1_out, not_1_out, Clock);
  and and_2 (and_2_out, Clock, Data);
  or or_1 (or_1_out, Clear, and_1_out);
  nor nor_1 (out_4, or_1_out, out_5);
  nor nor_2 (out_5, out_4, and_2_out);
endmodule

module \T_триггер  (
  input  Toggle,
  input  Clock,
  output out_3,
  output out_4
);

  wire nand_1_out, nand_2_out, nand_3_out, nand_4_out, nand_5_out, nand_6_out;

  nand nand_1 (nand_1_out, out_4, Toggle, Clock);
  nand nand_2 (nand_2_out, Clock, Toggle, out_3);
  nand nand_3 (nand_3_out, nand_1_out, nand_4_out);
  nand nand_4 (nand_4_out, nand_3_out, nand_2_out);
  nand nand_5 (nand_5_out, nand_1_out, nand_3_out);
  nand nand_6 (nand_6_out, nand_4_out, nand_2_out);
  nand nand_7 (out_3, nand_5_out, out_4);
  nand nand_8 (out_4, out_3, nand_6_out);
endmodule

module \Счетчик  (
  input  in_1,
  output [3:0] out_2
);

  wire clock_1_out, \jk_триггер_1_out_4 , \jk_триггер_2_out_4 , \jk_триггер_3_out_4 , \jk_триггер_4_out_4 ,
       not_1_out, not_3_out, not_4_out, not_5_out;

  Clock clock_1 (.out(clock_1_out));
  \JK_триггер  \jk_триггер_1  (
    .Jump(in_1), .Clock(clock_1_out), .Kill(in_1), .out_4(\jk_триггер_1_out_4 ));  // open: out_5
  \JK_триггер  \jk_триггер_2  (
    .Jump(in_1), .Clock(\jk_триггер_1_out_4 ), .Kill(in_1), .out_4(\jk_триггер_2_out_4 ));  // open: out_5
  \JK_триггер  \jk_триггер_3  (
    .Jump(in_1), .Clock(\jk_триггер_2_out_4 ), .Kill(in_1), .out_4(\jk_триггер_3_out_4 ));  // open: out_5
  not not_1 (not_1_out, \jk_триггер_3_out_4 );
  \JK_триггер  \jk_триггер_4  (
    .Jump(in_1), .Clock(\jk_триггер_3_out_4 ), .Kill(in_1), .out_4(\jk_триггер_4_out_4 ));  // open: out_5
  not not_2 (out_2[3], \jk_триггер_4_out_4 );
  not not_3 (not_3_out, not_1_out);
  and and_1 (out_2[2], not_3_out, not_4_out);
  not not_4 (not_4_out, out_2[3]);
  and and_2 (out_2[1], not_1_out, not_5_out);
  not not_5 (not_5_out, out_2[3]);

  assign out_2[0] = 1'b0;
endmodule

module \_8битный_регистр  (
  input  Clock,
  input  [7:0] in_2,
  input  Reset,
  output [7:0] out_4
);

  \D_триггер  \d_триггер_1  (.Clear(Reset), .Clock(Clock), .Data(in_2[0]), .out_4(out_4[0]));  // open: out_5
  \D_триггер  \d_триггер_2  (.Clear(Reset), .Clock(Clock), .Data(in_2[1]), .out_4(out_4[1]));  // open: out_5
  \D_триггер  \d_триггер_3  (.Clear(Reset), .Clock(Clock), .Data(in_2[2]), .out_4(out_4[2]));  // open: out_5
  \D_триггер  \d_триггер_4  (.Clear(Reset), .Clock(Clock), .Data(in_2[3]), .out_4(out_4[3]));  // open: out_5
  \D_триггер  \d_триггер_5  (.Clear(Reset), .Clock(Clock), .Data(in_2[4]), .out_4(out_4[4]));  // open: out_5
  \D_триггер  \d_триггер_6  (.Clear(Reset), .Clock(Clock), .Data(in_2[5]), .out_4(out_4[5]));  // open: out_5
  \D_триггер  \d_триггер_7  (.Clear(Reset), .Clock(Clock), .Data(in_2[6]), .out_4(out_4[6]));  // open: out_5
  \D_триггер  \d_триггер_8  (.Clear(Reset), .Clock(Clock), .Data(in_2[7]), .out_4(out_4[7]));  // open: out_5
endmodule

module \Память_4х4  (
  input  Reset,
  input  [7:0] in_2,
  input  in_3,
  input  [1:0] in_4,
  output [7:0] out_5
);

  wire demultiplexer_1_out0, demultiplexer_1_out1, demultiplexer_1_out2, demultiplexer_1_out3;
  wire [7:0] \n8битный_регистр_1_out_4 , \n8битный_регистр_2_out_4 , \n8битный_регистр_3_out_4 ,
       \n8битный_регистр_4_out_4 ;

  Demultiplexer #(.select(2)) demultiplexer_1 (
    .out0(demultiplexer_1_out0), .out1(demultiplexer_1_out1), .out2(demultiplexer_1_out2),
    .out3(demultiplexer_1_out3), .in(in_3), .sel(in_4));  // open: en
  \_8битный_регистр  \u_8битный_регистр_1  (
    .Clock(demultiplexer_1_out0), .in_2(in_2), .Reset(Reset), .out_4(\n8битный_регистр_1_out_4 ));
  \_8битный_регистр  \u_8битный_регистр_2  (
    .Clock(demultiplexer_1_out1), .in_2(in_2), .Reset(Reset), .out_4(\n8битный_регистр_2_out_4 ));
  \_8битный_регистр  \u_8битный_регистр_3  (
    .Clock(demultiplexer_1_out2), .in_2(in_2), .Reset(Reset), .out_4(\n8битный_регистр_3_out_4 ));
  \_8битный_регистр  \u_8битный_регистр_4  (
    .Clock(demultiplexer_1_out3), .in_2(in_2), .Reset(Reset), .out_4(\n8битный_регистр_4_out_4 ));
  Multiplexer #(.select(2), .width(8)) multiplexer_1 (
    .in0(\n8битный_регистр_1_out_4 ), .in1(\n8битный_регистр_2_out_4 ), .in2(\n8битный_регистр_3_out_4 ),
    .in3(\n8битный_регистр_4_out_4 ), .out(out_5), .sel(in_4));  // open: en
endmodule

module \Модиф__Сумматор  (
  input  Clock,
  input  [7:0] in_2,
  input  [7:0] in_3,
  input  Reset,
  input  in_5
);

  wire [7:0] adder_1_out, multiplexer_1_out, \n8битный_регистр_1_out_4 ;

  // Probe on in_3
  Multiplexer #(.width(8)) multiplexer_1 (
    .in0(in_3), .in1(\n8битный_регистр_1_out_4 ), .out(multiplexer_1_out), .sel(in_5));  // open: en
  // Probe on in_2
  // Probe on adder_1_out
  Adder adder_1 (.a(in_2), .b(multiplexer_1_out), .out(adder_1_out));  // open: cin, cout
  // Probe on \n8битный_регистр_1_out_4 
  \_8битный_регистр  \u_8битный_регистр_1  (
    .Clock(Clock), .in_2(adder_1_out), .Reset(Reset), .out_4(\n8битный_регистр_1_out_4 ));
endmodule

module \Память_на_32_байта  (
  input  Reset,
  input  [7:0] in_2,
  input  [2:0] \Х ,
  input  [1:0] in_4,
  input  in_5,
  output [7:0] out_6
);

  wire demultiplexer_1_out0, demultiplexer_1_out1, demultiplexer_1_out2, demultiplexer_1_out3,
       demultiplexer_1_out4, demultiplexer_1_out5, demultiplexer_1_out6, demultiplexer_1_out7;
  wire [7:0] \память_4х4_1_out_5 , \память_4х4_2_out_5 , \память_4х4_3_out_5 , \память_4х4_4_out_5 ,
       \память_4х4_5_out_5 , \память_4х4_6_out_5 , \память_4х4_7_out_5 , \память_4х4_8_out_5 ;

  Demultiplexer #(.select(3)) demultiplexer_1 (
    .out0(demultiplexer_1_out0), .out1(demultiplexer_1_out1), .out2(demultiplexer_1_out2),
    .out3(demultiplexer_1_out3), .out4(demultiplexer_1_out4), .out5(demultiplexer_1_out5),
    .out6(demultiplexer_1_out6), .out7(demultiplexer_1_out7), .in(in_5), .sel(\Х ));  // open: en
  \Память_4х4  \u_память_4х4_1  (
    .Reset(Reset), .in_2(in_2), .in_3(demultiplexer_1_out0), .in_4(in_4), .out_5(\память_4х4_1_out_5 ));
  \Память_4х4  \u_память_4х4_2  (
    .Reset(Reset), .in_2(in_2), .in_3(demultiplexer_1_out1), .in_4(in_4), .out_5(\память_4х4_2_out_5 ));
  \Память_4х4  \u_память_4х4_3  (
    .Reset(Reset), .in_2(in_2), .in_3(demultiplexer_1_out2), .in_4(in_4), .out_5(\память_4х4_3_out_5 ));
  \Память_4х4  \u_память_4х4_4  (
    .Reset(Reset), .in_2(in_2), .in_3(demultiplexer_1_out3), .in_4(in_4), .out_5(\память_4х4_4_out_5 ));
  \Память_4х4  \u_память_4х4_5  (
    .Reset(Reset), .in_2(in_2), .in_3(demultiplexer_1_out4), .in_4(in_4), .out_5(\память_4х4_5_out_5 ));
  \Память_4х4  \u_память_4х4_6  (
    .Reset(Reset), .in_2(in_2), .in_3(demultiplexer_1_out5), .in_4(in_4), .out_5(\память_4х4_6_out_5 ));
  \Память_4х4  \u_память_4х4_7  (
    .Reset(Reset), .in_2(in_2), .in_3(demultiplexer_1_out6), .in_4(in_4), .out_5(\память_4х4_7_out_5 ));
  \Память_4х4  \u_память_4х4_8  (
    .Reset(Reset), .in_2(in_2), .in_3(demultiplexer_1_out7), .in_4(in_4), .out_5(\память_4х4_8_out_5 ));
  Multiplexer #(.select(3), .width(8)) multiplexer_1 (
    .in0(\память_4х4_1_out_5 ), .in1(\память_4х4_2_out_5 ), .in2(\память_4х4_3_out_5 ),
    .in3(\память_4х4_4_out_5 ), .in4(\память_4х4_5_out_5 ), .in5(\память_4х4_6_out_5 ),
    .in6(\память_4х4_7_out_5 ), .in7(\память_4х4_8_out_5 ), .out(out_6), .sel(\Х ));  // open: en
endmodule
